// Logisim project Oblig1.circ as structural Verilog: 2 circuits, main circuit main
module main (
  input  in_1,
  input  in_2,
  input  in_3
);

  wire decoder_1_a, decoder_1_b, decoder_1_c, decoder_1_d, decoder_1_e, decoder_1_f, decoder_1_g;

  decoder decoder_1 (
    .x0(in_1), .x1(in_2), .x2(in_3), .a(decoder_1_a), .b(decoder_1_b), .c(decoder_1_c), .d(decoder_1_d),
    .e(decoder_1_e), .f(decoder_1_f), .g(decoder_1_g));
  _7_Segment_Display u_7_segment_display_1 (
    .g(decoder_1_g), .f(decoder_1_f), .a(decoder_1_a), .b(decoder_1_b), .e(decoder_1_e), .d(decoder_1_d),
    .c(decoder_1_c));  // open: dp
endmodule

module decoder (
  input  x0,
  input  x1,
  input  x2,
  output a,
  output b,
  output c,
  output d,
  output e,
  output f,
  output g
);

  wire and_1_out, and_2_out, and_3_out, and_4_out, and_5_out, and_6_out, and_7_out, not_1_out, not_2_out,
       not_3_out, not_4_out, not_5_out, not_6_out, not_7_out, not_8_out, not_9_out, not_10_out, not_11_out,
       not_12_out;

  not not_1 (not_1_out, x1);
  and and_1 (and_1_out, not_1_out, x2, not_2_out);
  not not_2 (not_2_out, x0);
  not not_3 (not_3_out, x0);
  not not_4 (not_4_out, x1);
  not not_5 (not_5_out, x2);
  not not_6 (not_6_out, x0);
  not not_7 (not_7_out, x2);
  not not_8 (not_8_out, x0);
  not not_9 (not_9_out, x1);
  not not_10 (not_10_out, x2);
  not not_11 (not_11_out, x1);
  not not_12 (not_12_out, x2);
  and and_2 (and_2_out, not_3_out, not_4_out, not_5_out);
  and and_3 (and_3_out, not_6_out, x1, not_7_out);
  and and_4 (and_4_out, not_8_out, x1, x2);
  and and_5 (and_5_out, x0, not_9_out, not_10_out);
  and and_6 (and_6_out, x0, not_11_out, x2);
  and and_7 (and_7_out, x0, x1, not_12_out);
  or or_1 (a, and_2_out, and_6_out, and_3_out, and_4_out);
  or or_2 (b, and_2_out, and_4_out, and_3_out, and_1_out, and_5_out);
  or or_3 (c, and_4_out, and_2_out, and_5_out, and_1_out, and_6_out, and_7_out);
  or or_4 (d, and_2_out, and_4_out, and_3_out, and_6_out, and_7_out);
  or or_5 (e, and_3_out, and_7_out, and_2_out);
  or or_6 (f, and_2_out, and_7_out, and_5_out, and_6_out);
  or or_7 (g, and_5_out, and_4_out, and_3_out, and_7_out, and_6_out);

  // Notes on the sheet:
  //   wrongly labeled
endmodule
