// Logisim project Oblig1B.circ as structural Verilog: 2 circuits, main circuit main
module main (
  input  in_1,
  input  in_2,
  input  in_3
);

  wire decoder_1_a, decoder_1_b, decoder_1_c, decoder_1_d, decoder_1_e, decoder_1_f, decoder_1_g;

  decoder decoder_1 (
    .x0(in_1), .x1(in_2), .x2(in_3), .a(decoder_1_a), .b(decoder_1_b), .c(decoder_1_c), .d(decoder_1_d),
    .e(decoder_1_e), .f(decoder_1_f), .g(decoder_1_g));
  _7_Segment_Display u_7_segment_display_1 (
    .g(decoder_1_g), .f(decoder_1_f), .a(decoder_1_a), .b(decoder_1_b), .e(decoder_1_e), .d(decoder_1_d),
    .c(decoder_1_c));  // open: dp
endmodule

module decoder (
  input  x0,
  input  x1,
  input  x2,
  output a,
  output b,
  output c,
  output d,
  output e,
  output f,
  output g
);

  wire and_1_out, and_2_out, and_3_out, and_4_out, and_5_out, and_6_out, and_7_out, not_1_out, not_2_out,
       not_3_out, undriven, undriven_2, undriven_3, undriven_4, undriven_5, undriven_6, undriven_7,
       undriven_8;

  not not_1 (not_1_out, x0);
  not not_2 (not_2_out, x1);
  not not_3 (not_3_out, x2);
  // AND_Gate and_1 has open pins: out=and_1_out
  // AND_Gate and_2 has open pins: out=and_2_out
  buf and_3 (and_3_out, undriven_8);  // AND_Gate
  and and_4 (and_4_out, undriven_4, undriven_3);
  buf and_5 (and_5_out, undriven_5);  // AND_Gate
  and and_6 (and_6_out, undriven_6, undriven);
  and and_7 (and_7_out, undriven_7, undriven_2);
  or or_1 (a, and_2_out, and_6_out, and_3_out, and_4_out);
  or or_2 (b, and_2_out, and_4_out, and_3_out, and_1_out, and_5_out);
  or or_3 (c, and_4_out, and_2_out, and_5_out, and_1_out, and_6_out, and_7_out);
  or or_4 (d, and_2_out, and_4_out, and_3_out, and_6_out, and_7_out);
  or or_5 (e, and_3_out, and_7_out, and_2_out);
  or or_6 (f, and_2_out, and_7_out, and_5_out, and_6_out);
  or or_7 (g, and_5_out, and_4_out, and_3_out, and_7_out, and_6_out);

  // Notes on the sheet:
  //   wrongly labeled
endmodule
