// Logisim project kodelaas_sindrech.circ as structural Verilog: 3 circuits, main circuit main
module main (
);

  wire clock_1_out, d0_q, d1_q, decorder_1_d0, decorder_1_d1, decorder_1_output, dekoder_1_x0, dekoder_1_x1,
       dekoder_1_x2;
  wire [6:0] _1_out;

  Button _1 (.out(_1_out[0]));
  Button _4 (.out(_1_out[3]));
  Button _7 (.out(_1_out[6]));
  Button button ();  // open: out
  Button _2 (.out(_1_out[1]));
  Button _5 (.out(_1_out[4]));
  Button _8 ();  // open: out
  Button _0 ();  // open: out
  Button _3 (.out(_1_out[2]));
  Button _6 (.out(_1_out[5]));
  Button _9 ();  // open: out
  Button button_2 ();  // open: out
  dekoder dekoder_1 (.in_1(_1_out), .x2(dekoder_1_x2), .x1(dekoder_1_x1), .x0(dekoder_1_x0));
  decorder decorder_1 (
    .q1(d1_q), .q0(d0_q), .x2(dekoder_1_x2), .x1(dekoder_1_x1), .x0(dekoder_1_x0), .d1(decorder_1_d1),
    .d0(decorder_1_d0), .\output (decorder_1_output));
  Clock clock_1 (.out(clock_1_out));
  D_Flip_Flop d1 (.clk(clock_1_out), .D(decorder_1_d1), .Q(d1_q));  // open: Qn, preset, en, reset
  D_Flip_Flop d0 (.clk(clock_1_out), .D(decorder_1_d0), .Q(d0_q));  // open: Qn, preset, en, reset
  LED led_1 (.in(decorder_1_output));

  // Notes on the sheet:
  //   code is 1, 2, 3
endmodule

module decorder (
  input  q1,
  input  q0,
  input  x2,
  input  x1,
  input  x0,
  output d1,
  output d0,
  output \output 
);

  wire and_1_out, and_2_out, and_3_out, and_4_out, and_5_out, and_6_out, and_7_out, and_8_out, not_1_out,
       not_2_out, not_3_out, not_4_out, not_5_out, not_6_out, not_7_out, not_8_out, not_9_out, not_10_out,
       not_11_out, not_12_out, not_13_out;

  not not_1 (not_1_out, x2);
  not not_2 (not_2_out, x0);
  not not_3 (not_3_out, q0);
  not not_4 (not_4_out, x2);
  not not_5 (not_5_out, x0);
  not not_6 (not_6_out, q1);
  not not_7 (not_7_out, x2);
  not not_8 (not_8_out, x1);
  not not_9 (not_9_out, x2);
  not not_10 (not_10_out, x0);
  not not_11 (not_11_out, q0);
  not not_12 (not_12_out, q0);
  not not_13 (not_13_out, x2);
  and and_1 (and_1_out, q0, not_1_out, x1, not_2_out);
  and and_2 (and_2_out, q1, not_3_out);
  and and_3 (and_3_out, q1, not_4_out, not_5_out);
  and and_4 (and_4_out, not_6_out, not_7_out, not_8_out, x0);
  and and_5 (and_5_out, q0, not_9_out, not_10_out);
  and and_6 (and_6_out, q1, not_11_out);
  and and_7 (and_7_out, q1, not_12_out);
  and and_8 (and_8_out, q1, not_13_out, x1, x0);
  or or_1 (d1, and_1_out, and_2_out, and_3_out);
  or or_2 (d0, and_4_out, and_5_out, and_6_out);
  or or_3 (\output , and_7_out, and_8_out);
endmodule

module dekoder (
  input  [6:0] in_1,
  output x2,
  output x1,
  output x0
);

  or or_1 (x2, in_1[6], in_1[5], in_1[4], in_1[3]);
  or or_2 (x1, in_1[6], in_1[5], in_1[2], in_1[1]);
  or or_3 (x0, in_1[6], in_1[4], in_1[2], in_1[0]);
endmodule
