// Logisim project oblig2.circ as structural Verilog: 3 circuits, main circuit main
module main (
);

  wire [3:0] decorder_1_x0, decorder_1_x1, decorder_1_x2;
  wire [11:0] _1_out;

  Button _1 (.out(_1_out[0]));
  Button _4 (.out(_1_out[3]));
  Button _7 (.out(_1_out[6]));
  Button button (.out(_1_out[9]));
  Button _2 (.out(_1_out[1]));
  Button _5 (.out(_1_out[4]));
  Button _8 (.out(_1_out[7]));
  Button _0 (.out(_1_out[10]));
  Button _3 (.out(_1_out[2]));
  Button _6 (.out(_1_out[5]));
  Button _9 (.out(_1_out[8]));
  Button button_2 (.out(_1_out[11]));
  decorder decorder_1 (.in_1(_1_out), .x2(decorder_1_x2), .x1(decorder_1_x1), .x0(decorder_1_x0));
  LED led_1 ();  // open: in
endmodule

module decorder (
  input  [11:0] in_1,
  output [3:0] x2,
  output [3:0] x1,
  output [3:0] x0
);

  wire and_1_out, and_2_out, and_3_out, and_4_out, not_1_out, not_2_out, not_3_out, not_4_out, or_1_out;
  wire [1:0] counter_1_q;
  wire [3:0] dekoder_1_out_2;

  or or_1 (or_1_out, in_1[0], in_1[1], in_1[2], in_1[3], in_1[4], in_1[5], in_1[7], in_1[8], in_1[9], in_1[10], in_1[11], in_1[6]);
  dekoder dekoder_1 (.in_1(in_1), .out_2(dekoder_1_out_2));
  Counter #(.width(2), .max('h3)) counter_1 (.Q(counter_1_q), .clk(or_1_out));  // open: load, D, count, carry, clr
  and and_1 (and_1_out, not_1_out, not_2_out);
  and and_2 (and_2_out, counter_1_q[0], counter_1_q[1]);
  not not_1 (not_1_out, counter_1_q[0]);
  not not_2 (not_2_out, counter_1_q[1]);
  Register #(.width(4)) register_1 (.D(dekoder_1_out_2), .Q(x2), .clk(and_4_out), .clr(and_2_out));  // open: en
  Register #(.width(4)) register_2 (.D(dekoder_1_out_2), .Q(x1), .clk(and_3_out), .clr(and_2_out));  // open: en
  Register #(.width(4)) register_3 (.D(dekoder_1_out_2), .Q(x0), .clk(and_1_out), .clr(and_2_out));  // open: en
  and and_3 (and_3_out, counter_1_q[0], not_4_out);
  not not_3 (not_3_out, counter_1_q[0]);
  not not_4 (not_4_out, counter_1_q[1]);
  and and_4 (and_4_out, not_3_out, counter_1_q[1]);
endmodule

module dekoder (
  input  [11:0] in_1,
  output [3:0] out_2
);

  or or_1 (out_2[3], in_1[8], in_1[7]);
  or or_2 (out_2[2], in_1[6], in_1[5], in_1[4], in_1[3]);
  or or_3 (out_2[1], in_1[6], in_1[5], in_1[2], in_1[1]);
  or or_4 (out_2[0], in_1[8], in_1[6], in_1[4], in_1[2], in_1[0]);
endmodule
