// Logisim project kodelaas_sindrech.circ as structural Verilog: 4 circuits, main circuit main
module main (
  output [11:0] out_1,
  output [3:0] out_2,
  output [3:0] out_3,
  output [3:0] out_4
);

  wire code_1_open;

  Button _1 (.out(out_1[0]));
  Button _4 (.out(out_1[3]));
  Button _7 (.out(out_1[6]));
  Button button (.out(out_1[9]));
  Button _2 (.out(out_1[1]));
  Button _5 (.out(out_1[4]));
  Button _8 (.out(out_1[7]));
  Button _0 (.out(out_1[10]));
  Button _3 (.out(out_1[2]));
  Button _6 (.out(out_1[5]));
  Button _9 (.out(out_1[8]));
  Button button_2 (.out(out_1[11]));
  decorder decorder_1 (.in_1(out_1), .x2(out_2), .x1(out_3), .x0(out_4));
  code code_1 (.x2(out_2), .x1(out_3), .x0(out_4), .open(code_1_open));
  LED led_1 (.in(code_1_open));

  // Notes on the sheet:
  //   to reset click the reset button
  //   must be reset for eatch try
  //   *,  0 and # is reset buttons
  //   code is 1, 2, 3
  //   reset
endmodule

module decorder (
  input  [11:0] in_1,
  output [3:0] x2,
  output [3:0] x1,
  output [3:0] x0
);

  wire and_1_out, and_2_out, and_3_out, not_1_out, not_2_out, not_3_out, not_4_out, not_5_out, or_1_out,
       or_2_out;
  wire [1:0] counter_1_q;
  wire [3:0] dekoder_1_out_2;

  or or_1 (or_1_out, in_1[0], in_1[1], in_1[2], in_1[3], in_1[4], in_1[5], in_1[7], in_1[8], in_1[9], in_1[10], in_1[11], in_1[6]);
  or or_2 (or_2_out, in_1[10], in_1[11], in_1[9]);
  dekoder dekoder_1 (.in_1(in_1), .out_2(dekoder_1_out_2));
  Counter #(.width(2), .max('h3), .ongoal("stay")) counter_1 (
    .Q(counter_1_q), .clk(or_1_out), .clr(or_2_out));  // open: load, D, count, carry
  and and_1 (and_1_out, not_1_out, not_3_out, not_2_out);
  not not_1 (not_1_out, counter_1_q[0]);
  not not_2 (not_2_out, counter_1_q[1]);
  not not_3 (not_3_out, or_2_out);
  Register #(.width(4), .trigger("falling")) register_1 (
    .D(dekoder_1_out_2), .Q(x2), .clk(and_3_out), .clr(or_2_out));  // open: en
  Register #(.width(4), .trigger("falling")) register_2 (
    .D(dekoder_1_out_2), .Q(x1), .clk(and_2_out), .clr(or_2_out));  // open: en
  Register #(.width(4), .trigger("falling")) register_3 (
    .D(dekoder_1_out_2), .Q(x0), .clk(and_1_out), .clr(or_2_out));  // open: en
  and and_2 (and_2_out, counter_1_q[0], not_4_out);
  not not_4 (not_4_out, counter_1_q[1]);
  not not_5 (not_5_out, counter_1_q[0]);
  and and_3 (and_3_out, not_5_out, counter_1_q[1]);
endmodule

module dekoder (
  input  [11:0] in_1,
  output [3:0] out_2
);

  or or_1 (out_2[3], in_1[8], in_1[7]);
  or or_2 (out_2[2], in_1[6], in_1[5], in_1[4], in_1[3]);
  or or_3 (out_2[1], in_1[6], in_1[5], in_1[2], in_1[1]);
  or or_4 (out_2[0], in_1[8], in_1[6], in_1[4], in_1[2], in_1[0]);
endmodule

module code (
  input  [3:0] x2,
  input  [3:0] x1,
  input  [3:0] x0,
  output open
);

  wire and_1_out, and_2_out, and_3_out, not_1_out, not_2_out, not_3_out, not_4_out, not_5_out, not_6_out,
       not_7_out, not_8_out;

  not not_1 (not_1_out, x2[2]);
  not not_2 (not_2_out, x2[3]);
  not not_3 (not_3_out, x1[0]);
  not not_4 (not_4_out, x1[2]);
  not not_5 (not_5_out, x0[1]);
  not not_6 (not_6_out, x0[2]);
  and and_1 (and_1_out, x2[0], x2[1], not_1_out, not_2_out);
  and and_2 (and_2_out, not_3_out, x1[1], not_4_out, not_7_out);
  not not_7 (not_7_out, x1[3]);
  and and_3 (and_3_out, x0[0], not_5_out, not_6_out, not_8_out);
  not not_8 (not_8_out, x0[3]);
  and and_4 (open, and_1_out, and_2_out, and_3_out);
endmodule
