// Logisim project Oblig1B.circ as structural Verilog: 2 circuits, main circuit main
module main (
  input  in_1,
  input  in_2,
  input  in_3
);

  wire decoder_1_a, decoder_1_b, decoder_1_c, decoder_1_d, decoder_1_e, decoder_1_f, decoder_1_g;

  decoder decoder_1 (
    .x2(in_1), .x1(in_2), .x0(in_3), .a(decoder_1_a), .b(decoder_1_b), .c(decoder_1_c), .d(decoder_1_d),
    .e(decoder_1_e), .f(decoder_1_f), .g(decoder_1_g));
  _7_Segment_Display u_7_segment_display_1 (
    .g(decoder_1_g), .f(decoder_1_f), .a(decoder_1_a), .b(decoder_1_b), .e(decoder_1_e), .d(decoder_1_d),
    .c(decoder_1_c));  // open: dp
endmodule

module decoder (
  input  x2,
  input  x1,
  input  x0,
  output a,
  output b,
  output c,
  output d,
  output e,
  output f,
  output g
);

  wire and_1_out, not_1_out, not_2_out, not_3_out, xnor_1_out;

  not not_1 (not_1_out, x2);
  not not_2 (not_2_out, x1);
  not not_3 (not_3_out, x0);
  NotExactlyOne xnor_1 (.out(xnor_1_out), .in0(x1), .in1(x2), .in2(x0));
  and and_1 (and_1_out, not_3_out, x1);
  or or_1 (a, xnor_1_out, and_1_out);

  // Notes on the sheet:
  //   wrongly labeled
endmodule
