// Logisim project Oblig1 in1020.circ as structural Verilog: 4 circuits, main circuit main
module main (
  input  [3:0] in_1,
  output [7:0] out_2
);

  ADDER adder_1 (.A4(in_1), .out_2(out_2));
endmodule

module Halvadder (
  input  A,
  input  B,
  output C,
  output S
);

  xor xor_1 (C, A, B);
  and and_1 (S, A, B);
endmodule

module ADDER (
  input  [3:0] A4,
  output [7:0] out_2
);

  wire fulladder_2_c, fulladder_3_c, fulladder_4_c, fulladder_5_c;

  fulladder fulladder_1 (.C(out_2[7]), .A(1'b0), .B(A4[3]), .S(out_2[6]), .Cn(fulladder_2_c));
  fulladder fulladder_2 (.C(fulladder_2_c), .A(A4[3]), .B(A4[2]), .S(out_2[5]), .Cn(fulladder_3_c));
  fulladder fulladder_3 (.C(fulladder_3_c), .A(A4[2]), .B(A4[1]), .S(out_2[4]), .Cn(fulladder_4_c));
  fulladder fulladder_4 (.C(fulladder_4_c), .A(A4[1]), .B(A4[0]), .S(out_2[3]), .Cn(fulladder_5_c));
  fulladder fulladder_5 (.C(fulladder_5_c), .A(A4[0]), .B(1'b0), .S(out_2[2]), .Cn(1'b0));

  assign out_2[1:0] = 2'b00;
endmodule

module fulladder (
  input  A,
  input  B,
  input  Cn,
  output C,
  output S
);

  wire and_1_out, and_2_out, xor_1_out;

  or or_1 (C, and_1_out, and_2_out);
  xor xor_1 (xor_1_out, A, B);
  and and_1 (and_1_out, A, B);
  xor xor_2 (S, xor_1_out, Cn);
  and and_2 (and_2_out, xor_1_out, Cn);
endmodule
