// Logisim project sindrech.circ as structural Verilog: 4 circuits, main circuit main
module main (
  input  [3:0] in_1,
  output [7:0] out_2
);

  ADDER adder_1 (.A4(in_1), .out_2(out_2));
endmodule

module ADDER (
  input  [3:0] A4,
  output [7:0] out_2
);

  wire fulladder_2_c, fulladder_3_c, fulladder_4_c, fulladder_5_c;

  fulladder fulladder_1 (.C(out_2[7]), .A(1'b0), .B(A4[3]), .S(out_2[6]), .Cn(fulladder_2_c));
  fulladder fulladder_2 (.C(fulladder_2_c), .A(A4[3]), .B(A4[2]), .S(out_2[5]), .Cn(fulladder_3_c));
  fulladder fulladder_3 (.C(fulladder_3_c), .A(A4[2]), .B(A4[1]), .S(out_2[4]), .Cn(fulladder_4_c));
  fulladder fulladder_4 (.C(fulladder_4_c), .A(A4[1]), .B(A4[0]), .S(out_2[3]), .Cn(fulladder_5_c));
  fulladder fulladder_5 (.C(fulladder_5_c), .A(A4[0]), .B(1'b0), .S(out_2[2]), .Cn(1'b0));

  assign out_2[1:0] = 2'b00;
endmodule

module fulladder (
  input  A,
  input  B,
  input  Cn,
  output C,
  output S
);

  wire and_1_out, and_2_out, xorboi_1_output;

  or or_1 (C, and_1_out, and_2_out);
  xorboi xorboi_1 (.in_1(B), .in_2(A), .\output (xorboi_1_output));
  and and_1 (and_1_out, A, B);
  xorboi xorboi_2 (.in_1(Cn), .in_2(xorboi_1_output), .\output (S));
  and and_2 (and_2_out, xorboi_1_output, Cn);
endmodule

module xorboi (
  input  in_1,
  input  in_2,
  output \output 
);

  wire and_2_out, not_1_out, or_1_out;

  and and_1 (\output , not_1_out, or_1_out);
  not not_1 (not_1_out, and_2_out);
  and and_2 (and_2_out, in_2, in_1);
  or or_1 (or_1_out, in_1, in_2);
endmodule
